# Fritzing sketch rc_boat (saved by Fritzing 0.9.3b)
perfboards: 1

parts:
  M1 = DC Motor
  Part1 = Arduino Nano (Rev3.0)
  LED1 = LED - 3mm [color="Red (633nm)" package="3 mm [THT]"]
  IC1 = L293D [package=THT]
  J1 = Basic Servo
  ANT1 = Antenna
  J2 = Buzzer
  U1 = XD-RF-5V [package=THT]
  C1 = Ceramic Capacitor [capacitance=100nF package="100 mil [THT, multilayer]"]
  VCC4 = Battery block 9V
  VCC6 = Battery
  C2 = Electrolytic Capacitor [capacitance=100µF package="200 mil [THT, electrolytic]"]
  C3 = Electrolytic Capacitor [capacitance=100µF package="200 mil [THT, electrolytic]"]

nets:
  N1: M1.pin_1, IC1.Out_1_(_Controlled_by_Enable_1_), C1.0
  N2: M1.pin_2, IC1.Out_2_(_Controlled_by_Enable_1_), C1.1
  GND: Part1.GND, LED1.cathode, IC1.0V, J2.pin1, U1.GND, VCC4.-, VCC6.-, C2.-, C3.-
  N3: Part1.D2, IC1.In_1
  N4: Part1.D3, J1.pulse
  N5: Part1.D4, IC1.In_2
  N6: Part1.D5, LED1.anode
  N7: Part1.D6, IC1.Enable_1
  N8: Part1.D9, J2.pin2
  N9: Part1.D11/MOSI, U1.DATA#1
  N10: Part1.VIN, VCC4.+
  N11: Part1.5V, IC1.+V
  N12: IC1.+Vmotor, J1.vcc, VCC6.+, C3.+
  N13: ANT1.antenna_lead, U1.Attenna
  N14: U1.VCC, C2.+

custom parts:
  Buzzer: Fixed frequency buzzer
  XD-RF-5V: This is 433Mhz RF transmitter with receiver kit for Arduino ARM MCU wireless Application environment: Remote control switch, receiver module, motorcycles, automobile anti-theft products, home security products, electric doors, shutter doors, windows, remote control socket, remote control LED, remote audio remote control electric doors, garage door remote control, remote control retractable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
  Battery: Your standard 2x 18650 battery pack (7,4 Volts)
