# Fritzing sketch rf_remote (saved by Fritzing 0.9.3b)
perfboards: 1

parts:
  S7 = Tactile Switch Buttons - 12mm Square [package=tactile-pth-12mm]
  S9 = Tactile Switch Buttons - 12mm Square [package=tactile-pth-12mm]
  S10 = Tactile Switch Buttons - 12mm Square [package=tactile-pth-12mm]
  Part2 = Arduino Nano (Rev3.0)
  S8 = Tactile Switch Buttons - 12mm Square [package=tactile-pth-12mm]
  U1 = FS1000A - 433Mhz RF Transmitter [package=THT]
  VCC1 = 4 x AA Battery Mount

nets:
  N1: S7.1, S7.3, Part2.D4
  N2: S7.2, S7.4
  N3: S9.1, S9.3
  N4: S9.2, S9.4, Part2.D6
  N5: S10.1, S10.3, Part2.D2
  N6: S10.2, S10.4
  N7: Part2.GND, S8.2, S8.4, VCC1.-
  N8: Part2.D8, S8.1, S8.3
  N9: Part2.D12/MISO, U1.DATA
  N10: Part2.VIN, VCC1.+
  5V: Part2.5V, U1.VCC

custom parts:
  Tactile Switch Buttons - 12mm Square: Medium-sized clicky momentary switches are standard input "buttons" on electronic projects. These work best in a PCB but can be used on a solderless breadboard as shown in this tutorial. The pins are normally open (disconnected) and when the button is pressed they are momentarily closed. They come in a pack of 10, they're pretty handy so you'll want to keep them around. You can find an EAGLE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
  FS1000A - 433Mhz RF Transmitter: This is 433Mhz RF transmitter with receiver kit for Arduino ARM MCU wireless Application environment: Remote control switch, receiver module, motorcycles, automobile anti-theft products, home security products, electric doors, shutter doors, windows, remote control socket, remote control LED, remote audio remote control electric doors, garage door remote control, remote control retractable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
  4 x AA Battery Mount: A 4 x AA battery pack (4.8 Volts with recharables)
